# Fritzing sketch schematic (saved by Fritzing 0.9.3b)
breadboards: 1

parts:
  part = ESP32-38PinWide
  LCD1 = 20x4 LCD display [part_number=2004A]
  part_2 = TRIMPOT [package=trim_pot_pth]
  part_3 = Resistor [tolerance=±5% resistance=4.7k package=THT]
  rotation_sensor = male pin header, 2 pins [form="♂ (male)"]
  Inc = SWITCH-MOMENTARY-2 [package=tactile-pth-12mm]
  Dec = SWITCH-MOMENTARY-2 [package=tactile-pth-12mm]

nets:
  N1: part.GPIO32, LCD1.DB7
  N2: part.GPIO33, LCD1.DB6
  N3: part.GPIO25, LCD1.A_+
  N4: part.GPIO26, LCD1.DB5
  N5: part.GPIO27, LCD1.DB4
  N6: part.GPIO14, LCD1.E
  GND: part.GND, LCD1.Vss, LCD1.R/W, LCD1.K_-, part_2.CW, part_3.Pin_0, rotation_sensor.pin1, Dec.1
  VIN: part.VIN, LCD1.Vdd, part_2.CCW
  N7: part.GPIO2, Dec.2
  N8: part.GPIO0, Inc.2
  N9: part.GPIO23, rotation_sensor.pin2
  N10: LCD1.Vo, part_2.WIPER
  N11: LCD1.RS, part_3.Pin_1

custom parts:
  ESP32-38PinWide: Generic 38-Pin ESP32 with wide format (only access to one side of pins on a breadboard) based on Stephen Lilley's HiLetgo ESP-WROOM-32 ESP32 ESP-32S Development Board.
  20x4 LCD display: 20x4 character display. CHECK LED POLARITY BEFORE CONNECTING POWER Some versions of the dispaly have the polarity of the LED pins "A" and "K" reversed.
